// Logisim project cdm-platform.circ as structural Verilog: 1 circuit, main circuit Main
module Main (
);

  wire cdm_8_mark5_1_data_inst, Clock, Data, DOWN, HIT, I_O, IAck, Inst, IR_Enable,
       ir_enable_buffer_1_int0_2, ir_enable_buffer_1_int1_2, ir_enable_buffer_1_int2_2,
       ir_enable_buffer_1_int3_2, ir_enable_buffer_1_int4_2, ir_enable_buffer_1_int5_2,
       ir_enable_buffer_1_int6_2, ir_enable_buffer_1_int7_2, irarb_1_ia0, irarb_1_ia1, irarb_1_ia2,
       irarb_1_ia3, irarb_1_ia4, irarb_1_ia5, irarb_1_ia6, irarb_1_ia7, IRQ, kA, kC, kE, LEFT, mem,
       not_1_out, RAM, rd_wr_prime, RIGHT, ROM, tCk, tCr, tE, UP, Vector;
  wire [2:0] vec;
  wire [3:0] I_O_Address;
  wire [6:0] kD, tD;
  wire [7:0] Address_Bus, cdm_8_mark5_1_data_out, controlled_buffer_1_out, Data_Bus, io_reg_1_data_out, PC,
       PS, R0, R1, R2, R3, ROM_Address_Hi, SP;
  wire [11:0] RAM_Address;
  wire [31:0] display_controller_color_1_colomn_scan_b, display_controller_color_1_colomn_scan_g,
       display_controller_color_1_colomn_scan_r, display_controller_color_1_data_blue,
       display_controller_color_1_data_green, display_controller_color_1_data_red,
       display_controller_color_2_colomn_scan_b, display_controller_color_2_colomn_scan_g,
       display_controller_color_2_colomn_scan_r, display_controller_color_2_data_blue,
       display_controller_color_2_data_green, display_controller_color_2_data_red;

  Clock clock_1 (.out(Clock));
  IrArb irarb_1 (
    .IAck(IAck), .Vector(vec), .IRQ(IRQ), .INT0(ir_enable_buffer_1_int0_2), .IA0(irarb_1_ia0),
    .INT1(ir_enable_buffer_1_int1_2), .IA1(irarb_1_ia1), .INT2(ir_enable_buffer_1_int2_2), .IA2(irarb_1_ia2),
    .INT3(ir_enable_buffer_1_int3_2), .IA3(irarb_1_ia3), .INT4(ir_enable_buffer_1_int4_2), .IA4(irarb_1_ia4),
    .INT5(ir_enable_buffer_1_int5_2), .IA5(irarb_1_ia5), .INT6(ir_enable_buffer_1_int6_2), .IA6(irarb_1_ia6),
    .INT7(ir_enable_buffer_1_int7_2), .IA7(irarb_1_ia7));
  Ir_Enable_Buffer ir_enable_buffer_1 (
    .Data_Bus_In(Data_Bus), .rd_wr_prime(rd_wr_prime), .IO_Address(I_O_Address), .IO(I_O),
    .Device_Address(4'b0000), .Clock(Clock), .Data_Bus_Out(Data_Bus), .INT0(UP), .INT1(DOWN), .INT2(LEFT),
    .INT3(RIGHT), .INT4(HIT), .INT0_2(ir_enable_buffer_1_int0_2), .IA0(irarb_1_ia0),
    .INT1_2(ir_enable_buffer_1_int1_2), .IA1(irarb_1_ia1), .INT2_2(ir_enable_buffer_1_int2_2),
    .IA2(irarb_1_ia2), .INT3_2(ir_enable_buffer_1_int3_2), .IA3(irarb_1_ia3),
    .INT4_2(ir_enable_buffer_1_int4_2), .IA4(irarb_1_ia4), .INT5_2(ir_enable_buffer_1_int5_2),
    .IA5(irarb_1_ia5), .INT6_2(ir_enable_buffer_1_int6_2), .IA6(irarb_1_ia6),
    .INT7_2(ir_enable_buffer_1_int7_2), .IA7(irarb_1_ia7), .Enable(IR_Enable));  // open: IA0_2, IA1_2, IA2_2, IA3_2, IA4_2, INT5, IA5_2, INT6, IA6_2, INT7, IA7_2
  Terminal_Controller terminal_controller_1 (
    .Clock(Clock), .rd_wr_prime(rd_wr_prime), .IO_Address(I_O_Address), .IO(I_O), .Keyboard_Enable(kE),
    .Device_Address(4'b0100), .Keyboard_Clock(kC), .Keyboard_Data(kD), .Keyboard_Available(kA),
    .Data_Bus_In(Data_Bus), .Data_Bus_Out(Data_Bus), .Terminal_Data(tD), .Terminal_Clear(tCr),
    .Terminal_Clock(tCk), .Terminal_Enable(tE));  // open: IRQ
  RAM #(.addrWidth(12)) ram_1 (
    .addr(RAM_Address), .data(Data_Bus), .sel(RAM), .clk(Clock), .ld(rd_wr_prime));  // open: clr
  IO_Random_Number_Generator io_random_number_generator_1 (
    .Clock(Clock), .rd_wr_prime(rd_wr_prime), .IO_Address(I_O_Address), .IO(I_O), .Device_Address(4'b0001),
    .Data_Bus_Out(Data_Bus));
  RAM_Controller ram_controller_1 (
    .Clock(Clock), .rd_wr_prime(rd_wr_prime), .IO_Address(I_O_Address), .IO(I_O), .Device_Address(4'b1110),
    .Data_Bus_In(Data_Bus), .Data_Bus_Out(Data_Bus), .Address_Bus(Address_Bus), .RAM_Address(RAM_Address));
  CdM_8_mark5 cdm_8_mark5_1 (
    .clock(Clock), .addr(Address_Bus), .mem_read(rd_wr_prime), .mem_cycle(mem),
    .data_inst(cdm_8_mark5_1_data_inst), .data_out(cdm_8_mark5_1_data_out),
    .data_in(controlled_buffer_1_out), .r0(R0), .r1(R1), .r2(R2), .r3(R3), .PC(PC), .SP(SP), .PS(PS),
    .IAck(IAck), .IRQ(IRQ), .vec(vec));
  assign controlled_buffer_1_out = rd_wr_prime ? Data_Bus : 8'bz;  // Controlled_Buffer controlled_buffer_1
  Address_Decoder address_decoder_1 (
    .data_ins_prime(cdm_8_mark5_1_data_inst), .memory(mem), .Address_Bus(Address_Bus), .Inst(Inst),
    .Data(Data), .Vector(Vector), .I_O(I_O), .ROM(ROM), .I_O_Address(I_O_Address), .RAM(RAM),
    .I_O_Offset(4'b0111));
  assign Data_Bus = not_1_out ? cdm_8_mark5_1_data_out : 8'bz;  // Controlled_Buffer controlled_buffer_2
  not not_1 (not_1_out, rd_wr_prime);
  // RAM ram_2: pin names not known; wires that end beside it: {ROM_Address_Hi[6:0], Address_Bus}, ROM, Data_Bus
  IO_Reg io_reg_1 (
    .Data_Bus_In(Data_Bus), .rd_wr_prime(rd_wr_prime), .IO_Address(I_O_Address), .IO(I_O),
    .Device_Address(4'b0010), .Clock(Clock), .Data_Bus_Out(Data_Bus), .Data_Out(io_reg_1_data_out));
  ROM_Controller rom_controller_1 (
    .Clock(Clock), .rd_wr_prime(rd_wr_prime), .IO_Address(I_O_Address), .IO(I_O), .Device_Address(4'b1000),
    .ISR_Bank(io_reg_1_data_out), .Data_Bus_In(Data_Bus), .Data_Bus_Out(Data_Bus),
    .Addrerss_Out(ROM_Address_Hi), .IAck(IAck), .IR_Enable(IR_Enable));
  Display_Controller_Color display_controller_color_1 (
    .Data_Bus_In(Data_Bus), .Data_Bus_Out(Data_Bus), .Clock(Clock), .rd_wr_prime(rd_wr_prime),
    .IO_Address(I_O_Address), .IO(I_O), .Device_Address(4'b1010), .Fast_Clock(Clock),
    .Data_Red(display_controller_color_1_data_red), .Data_Green(display_controller_color_1_data_green),
    .Colomn_Scan_R(display_controller_color_1_colomn_scan_r),
    .Data_Blue(display_controller_color_1_data_blue),
    .Colomn_Scan_G(display_controller_color_1_colomn_scan_g),
    .Colomn_Scan_B(display_controller_color_1_colomn_scan_b));
  // DotMatrix #(.inputtype("select"), .matrixcols(32), .matrixrows(32), .persist(64)) dotmatrix_1: pin names not known; wires that end beside it: display_controller_color_1_colomn_scan_r, display_controller_color_1_data_red
  // DotMatrix #(.inputtype("select"), .matrixcols(32), .matrixrows(32), .persist(64)) dotmatrix_2: pin names not known; wires that end beside it: display_controller_color_1_colomn_scan_g, display_controller_color_1_data_green
  // DotMatrix #(.inputtype("select"), .matrixcols(32), .matrixrows(32), .persist(64)) dotmatrix_3: pin names not known; wires that end beside it: display_controller_color_1_colomn_scan_b, display_controller_color_1_data_blue
  TTY tty_1 (.data(tD), .clk(tCk), .we(tE), .clr(tCr));
  Keyboard keyboard_1 (.clk(kC), .re(kE), .avail(kA), .data(kD));  // open: clr
  Display_Controller_Color display_controller_color_2 (
    .Data_Bus_In(Data_Bus), .Data_Bus_Out(Data_Bus), .Clock(Clock), .rd_wr_prime(rd_wr_prime),
    .IO_Address(I_O_Address), .IO(I_O), .Device_Address(4'b1011), .Fast_Clock(Clock),
    .Data_Red(display_controller_color_2_data_red), .Data_Green(display_controller_color_2_data_green),
    .Colomn_Scan_R(display_controller_color_2_colomn_scan_r),
    .Data_Blue(display_controller_color_2_data_blue),
    .Colomn_Scan_G(display_controller_color_2_colomn_scan_g),
    .Colomn_Scan_B(display_controller_color_2_colomn_scan_b));
  // DotMatrix #(.inputtype("select"), .matrixcols(32), .matrixrows(32), .persist(64)) dotmatrix_4: pin names not known; wires that end beside it: display_controller_color_2_colomn_scan_g, display_controller_color_2_data_green
  // DotMatrix #(.inputtype("select"), .matrixcols(32), .matrixrows(32), .persist(64)) dotmatrix_5: pin names not known; wires that end beside it: display_controller_color_2_colomn_scan_b, display_controller_color_2_data_blue
  // DotMatrix #(.inputtype("select"), .matrixcols(32), .matrixrows(32), .persist(64)) dotmatrix_6: pin names not known; wires that end beside it: display_controller_color_2_colomn_scan_r, display_controller_color_2_data_red
  Button button_1 (.out(LEFT));
  Button button_2 (.out(UP));
  Button button_3 (.out(DOWN));
  Button button_4 (.out(RIGHT));
  Button button_5 (.out(HIT));
  // Probe on R0
  // Probe on R0
  // Probe on R1
  // Probe on R1
  // Probe on R2
  // Probe on R2
  // Probe on R3
  // Probe on R3
  // Probe on R0
  // Probe on R0
  // Probe on R1
  // Probe on R1
  // Probe on R2
  // Probe on R2
  // Probe on R3
  // Probe on R3
  // Probe on PC
  // Probe on PC
  // Probe on SP
  // Probe on SP
  // Probe on PC
  // Probe on SP
  // Probe on PS

  // Notes on the sheet:
  //   Interrupts
  //   RAM
  //   IO Bus
  //   ROM
  //   User Area
endmodule
